# Fritzing sketch quattro_led (saved by Fritzing 0.9.0b)
breadboards: 1

parts:
  Part1 = Arduino Uno (Rev3)
  LED1 = LED - 5mm [color="Red (633nm)" package="5 mm [THT]"]
  LED2 = LED - 5mm [color="Yellow (592nm)" package="5 mm [THT]"]
  LED3 = LED - 5mm [color="Blue (505nm)" package="5 mm [THT]"]
  LED4 = LED - 5mm [color="Green (560nm)" package="5 mm [THT]"]
  R1 = Resistor [tolerance=±5% resistance=220 package=THT]
  R2 = Resistor [tolerance=±5% resistance=220 package=THT]
  R3 = Resistor [tolerance=±5% resistance=220 package=THT]
  R4 = Resistor [tolerance=±5% resistance=220 package=THT]

nets:
  N1: Part1.D10_PWM/SS, R4.Pin_0
  N2: Part1.D11_PWM/MOSI, R2.Pin_0
  N3: Part1.D12/MISO, R3.Pin_0
  N4: Part1.D13/SCK, R1.Pin_0
  N5: Part1.GND, LED2.cathode, LED3.cathode, LED4.cathode
  N6: LED1.anode, R1.Pin_1
  N7: LED2.anode, R3.Pin_1
  N8: LED3.anode, R2.Pin_1
  N9: LED4.anode, R4.Pin_1
