# Fritzing sketch rele_con_bjt (saved by Fritzing 0.9.0b)
breadboards: 1

parts:
  Part1 = Arduino Uno (Rev3)
  Q1 = NPN-Transistor [package="TO92 [THT]"]
  U1 = RELAY [package=relay-g5q]
  R1 = Resistor [tolerance=±5% resistance=47 package=THT]
  D1 = Rectifier Diode [part_number=1N4001 package="300 mil [THT]"]
  VCC1 = Battery block 9V
  Q2 = NPN-Transistor [package="TO92 [THT]"]  # not connected

nets:
  N1: Part1.D13/SCK, R1.Pin_0
  N2: Part1.GND, Q1.E, VCC1.-
  N3: Q1.B, R1.Pin_1
  N4: Q1.C, U1.COIL1, D1.anode
  N5: U1.COIL2, D1.cathode, VCC1.+

notes:
  Relè 9V
  Transistor NPN
  E B C
