# Fritzing sketch mosfet_motore (saved by Fritzing 0.9.0b)
breadboards: 1

parts:
  Part1 = Arduino Uno (Rev3)
  R1 = Resistor [tolerance=±5% resistance=10k package=THT]
  D1 = Rectifier Diode [part_number=1N4001 package="300 mil [THT]"]
  Q1 = Basic FET N-Channel [package="TO220 [THT]"]
  M1 = DC Motor
  Power_plug1 = Power plug
  Q2 = Basic FET N-Channel [package="TO220 [THT]"]  # not connected

nets:
  N1: Part1.D13/SCK, R1.Pin_1, Q1.gate
  GND: Part1.GND, R1.Pin_0, Q1.source, Power_plug1.GND
  N2: D1.cathode, M1.pin_2, Power_plug1.VCC
  N3: D1.anode, Q1.drain, M1.pin_1

notes:
  IRF520
  G D S
  Alimentazione 12V
  Motore corrente continua a 12V
