# Fritzing sketch 037-fotoresistenza_e_led (saved by Fritzing 0.9.0b)
breadboards: 1

parts:
  R1 = Resistor [tolerance=±5% resistance=1k package=THT]
  Part1 = Arduino Uno (Rev3)
  R2 = Photocell (LDR) [package=THT]
  LED1 = LED - 5mm [color="Red (633nm)" package="5 mm [THT]"]
  R3 = Resistor [tolerance=±5% resistance=390 package=THT]

nets:
  N1: R1.Pin_0, Part1.A0, R2.pin_1
  N2: R1.Pin_1, Part1.GND, LED1.cathode
  N3: Part1.D13/SCK, R3.Pin_1
  N4: Part1.5V, R2.pin_0
  N5: LED1.anode, R3.Pin_0
