# Fritzing sketch 040-trimmer_e_led (saved by Fritzing 0.9.0b)
breadboards: 1

parts:
  Part1 = Arduino Uno (Rev3)
  LED1 = LED - 5mm [color="Red (633nm)" package="5 mm [THT]"]
  R3 = Resistor [tolerance=±5% resistance=390 package=THT]
  R4 = Trimmer Potentiometer [maximum_resistance=10kΩ package=THT]

nets:
  N1: Part1.A0, R4.wiper
  N2: Part1.D13/SCK, R3.Pin_1
  N3: Part1.GND, LED1.cathode, R4.leg1
  N4: Part1.5V, R4.leg2
  N5: LED1.anode, R3.Pin_0

notes:
  termistore
