# Fritzing sketch 041-tilt (saved by Fritzing 0.9.0b)
breadboards: 1

parts:
  R1 = Resistor [tolerance=±5% resistance=10k package=THT]
  Part1 = Arduino Uno (Rev3)
  LED1 = LED - 5mm [color="Red (633nm)" package="5 mm [THT]"]
  R3 = Resistor [tolerance=±5% resistance=390 package=THT]
  S1 = Tilt Switch [package=THT]

nets:
  N1: R1.Pin_0, Part1.D8, S1.Pin_2
  N2: R1.Pin_1, Part1.GND, LED1.cathode
  N3: Part1.D12/MISO, R3.Pin_1
  N4: Part1.5V, S1.Pin_1
  N5: LED1.anode, R3.Pin_0
