# Fritzing sketch 040-PIR (saved by Fritzing 0.9.0b)
breadboards: 1

parts:
  Part1 = Arduino Uno (Rev3)
  LED1 = LED - 5mm [color="Red (633nm)" package="5 mm [THT]"]
  R3 = Resistor [tolerance=±5% resistance=390 package=THT]
  U1 = LM34 [package=so08]

nets:
  N1: Part1.D13/SCK, R3.Pin_1
  GND: Part1.GND, LED1.cathode, U1.GND
  N2: Part1.D7, U1.VOUT
  N3: Part1.5V, U1.V+
  N4: LED1.anode, R3.Pin_0

notes:
  PIR con uscita digitale
