# Fritzing sketch coppia_arduino_serialsoftware_bb (saved by Fritzing 0.9.0b)

parts:
  Part1 = Arduino Uno (Rev3)
  Part2 = Arduino Uno (Rev3)

nets:
  N1: Part1.D0/RX, Part2.D11_PWM/MOSI
  N2: Part1.D1/TX, Part2.D10_PWM/SS
