# Fritzing sketch 054-opto-in (saved by Fritzing 0.9.0b)
breadboards: 1

parts:
  Part1 = Arduino Uno (Rev3)
  U1 = Optocoupler [package=THT]
  S1 = Pushbutton [package="[THT]"]
  LED1 = LED - 5mm [color="Red (633nm)" package="5 mm [THT]"]
  VCC1 = 4 x AAA Battery Mount
  R1 = Resistor [tolerance=±5% resistance=390 package=THT]
  R2 = Resistor [tolerance=±5% resistance=10k package=THT]
  LED2 = LED - 5mm [color="Green (565nm)" package="5 mm [THT]"]
  R3 = Resistor [tolerance=±5% resistance=390 package=THT]

nets:
  N1: Part1.D13/SCK, LED2.anode
  N2: Part1.GND, U1.Pin_4, R3.Pin_1
  N3: Part1.D2, U1.Pin_5, R2.Pin_1
  N4: Part1.5V, R2.Pin_0
  N5: U1.Pin_1, S1.Pin_1, S1.Pin_2
  N6: U1.Pin_2, VCC1.-
  N7: S1.Pin_3, S1.Pin_4, LED1.cathode
  N8: LED1.anode, R1.Pin_1
  N9: VCC1.+, R1.Pin_0
  N10: LED2.cathode, R3.Pin_0
