# Fritzing sketch 056-opto-out (saved by Fritzing 0.9.0b)
breadboards: 1

parts:
  Part1 = Arduino Uno (Rev3)
  U1 = Optocoupler [package=THT]
  LED1 = LED - 5mm [color="Red (633nm)" package="5 mm [THT]"]
  VCC1 = 4 x AAA Battery Mount
  R1 = Resistor [tolerance=±5% resistance=390 package=THT]
  LED2 = LED - 5mm [color="Green (565nm)" package="5 mm [THT]"]
  R3 = Resistor [tolerance=±5% resistance=390 package=THT]

nets:
  N1: Part1.D13/SCK, LED2.anode
  N2: Part1.GND, U1.Pin_2
  N3: U1.Pin_1, R3.Pin_1
  N4: U1.Pin_4, VCC1.-
  N5: U1.Pin_5, LED1.cathode
  N6: LED1.anode, R1.Pin_1
  N7: VCC1.+, R1.Pin_0
  N8: LED2.cathode, R3.Pin_0
