# Fritzing sketch servomotore360 (saved by Fritzing 0.9.0b)
breadboards: 1

parts:
  Part1 = Arduino Uno (Rev3)
  J1 = Basic Servo

nets:
  GND: Part1.GND, J1.gnd
  N1: Part1.D7, J1.pulse
  5V: Part1.5V, J1.vcc
